# Fritzing sketch SBSMark3 (saved by Fritzing 0.9.3b)
circuit board: 8.46667cm x 5.64444cm
breadboards: 1

parts:
  ESP32 = Adafruit HUZZAH32 ESP32 Feather [part_number="Adafruit #3405"]
  IMU = GY-521 (MPU-6050) [form="♀ (female)" package=THT]
  LCD = LCD1602-I2C
  12to5VCD = Mini-360 DC-DC Buck converter [package=THT]
  USB_Micro_B = USB_MICROB_PLUG [package=micro-b-smt]
  PWR_Jack = Power Jack [package=power_jack_slot]
  S1 = Taiway 100-SP-X-T1 SPDT Miniature Toggle Switch [part_number=100-SP-X-T1-0-0-B1-M2 package=THT]
  S2 = Taiway 100-SP-X-T1 SPDT Miniature Toggle Switch [part_number=100-SP-X-T1-0-0-B1-M2 package=THT]
  BATT1 = LiPoly Battery (1300mAh)

nets:
  N1: ESP32.GND, IMU.pin2, IMU.pin7
  N2: ESP32.3.3V, IMU.pin1
  N3: ESP32.SCL, IMU.pin3, LCD.SCL
  N4: ESP32.SDA, IMU.pin4, LCD.SDA
  GND: LCD.GND, 12to5VCD.OUT-, USB_Micro_B.GND, BATT1.negative
  N5: LCD.VCC, S1.COM
  N6: 12to5VCD.IN-, PWR_Jack.GND
  N7: 12to5VCD.IN+, S2.COM
  N8: 12to5VCD.OUT+, S1.L1
  N9: USB_Micro_B.VCC, S1.L2
  N10: PWR_Jack.GNDBREAK, S2.L1
  N11: S2.L2, BATT1.positive

custom parts:
  GY-521 (MPU-6050): Placa GY-521 basada en conjunto de acelerómetro+giroscopios MPU-6050
  LCD1602-I2C: A standard character display, usually with 2x16 characters. Comes in many colors with LCM1602 IIC attached.
  Mini-360 DC-DC Buck converter: Mini-360 DC-DC Buck converter. Tiny buck step down voltage converter, input voltage 4.75 to 23V output 1 to 17V adjustable. Available from ebay and the like.
  LiPoly Battery (1300mAh): Lithium Ion Polymer Battery (1300mAh)
